// Logisim project BACKUP.circ as structural Verilog: 1 circuit, main circuit main
module main (
);

  wire and_1_out, and_2_out, clock_1_out, comparator_1_eq, comparator_2_eq, comparator_3_eq, comparator_4_eq,
       comparator_5_eq, comparator_6_eq, pc_carry, pull_resistor_1_node, pull_resistor_2_node,
       pull_resistor_3_node, pull_resistor_4_node, RESET_out, STEP_out;
  wire [1:0] counter_1_q;
  wire [3:0] REG_A_q, REG_A_q_2, REG_B_q, REG_B_q_2, REG_C_q, REG_C_q_2;
  wire [7:0] adder_1_out, controlled_buffer_1_out, prog_data, subtractor_1_out, undriven, undriven_2;
  wire [15:0] pc_q;

  Clock clock_1 (.out(clock_1_out));
  Pull_Resistor pull_resistor_1 (.node(pull_resistor_1_node));
  buf buffer_1 (pull_resistor_1_node, clock_1_out);
  buf buffer_2 (pull_resistor_1_node, STEP_out);
  Counter #(.max('h3), .width(2)) counter_1 (
    .clr(RESET_out), .clk(pull_resistor_1_node), .D(2'b00), .Q(counter_1_q));  // open: load, up, count, carry
  Button RESET (.out(RESET_out));
  Comparator #(.width(2)) comparator_1 (.a(2'b00), .b(counter_1_q), .eq(comparator_1_eq));  // open: gt, lt
  Counter #(.max('hffff), .width(16)) pc (
    .clr(RESET_out), .clk(comparator_1_eq), .carry(pc_carry), .Q(pc_q));  // open: load, up, count, D
  LED overflow (.in(pc_carry));
  Button STEP (.out(STEP_out));
  ROM #(.addrWidth(16)) prog (.addr(pc_q), .data(prog_data));
  Hex_Digit_Display hex_digit_display_1 (.value(REG_A_q_2));  // open: dp
  Hex_Digit_Display hex_digit_display_2 (.value(REG_B_q_2));  // open: dp
  Hex_Digit_Display hex_digit_display_3 (.value(REG_C_q_2));  // open: dp
  Hex_Digit_Display hex_digit_display_4 (.value(REG_A_q));  // open: dp
  Hex_Digit_Display hex_digit_display_5 (.value(REG_B_q));  // open: dp
  Hex_Digit_Display hex_digit_display_6 (.value(REG_C_q));  // open: dp
  Register REG_A (
    .D(controlled_buffer_1_out), .clk(pull_resistor_2_node), .Q({REG_A_q_2, REG_A_q}), .clr(RESET_out));  // open: en
  LED led_1 (.in(pull_resistor_2_node));
  Register REG_B (.D(undriven), .clk(pull_resistor_3_node), .Q({REG_B_q_2, REG_B_q}), .clr(RESET_out));  // open: en
  LED led_2 (.in(pull_resistor_3_node));
  Register REG_C (.D(undriven_2), .clk(pull_resistor_4_node), .Q({REG_C_q_2, REG_C_q}), .clr(RESET_out));  // open: en
  LED led_3 (.in(pull_resistor_4_node));
  Pull_Resistor pull_resistor_2 (.node(pull_resistor_2_node));
  Pull_Resistor pull_resistor_3 (.node(pull_resistor_3_node));
  Pull_Resistor pull_resistor_4 (.node(pull_resistor_4_node));
  Comparator comparator_2 (.a(prog_data), .b({8{1'b0}}), .eq(comparator_2_eq));  // open: gt, lt
  LED NOOP (.in(comparator_2_eq));
  Comparator comparator_3 (.a(prog_data), .b(8'h1), .eq(comparator_3_eq));  // open: gt, lt
  LED ADD (.in(comparator_3_eq));
  assign controlled_buffer_1_out = comparator_3_eq ? adder_1_out : 8'bz;  // Controlled_Buffer controlled_buffer_1
  Comparator comparator_4 (.a(prog_data), .b(8'h2), .eq(comparator_4_eq));  // open: gt, lt
  LED SUB (.in(comparator_4_eq));
  assign controlled_buffer_1_out = comparator_4_eq ? subtractor_1_out : 8'bz;  // Controlled_Buffer controlled_buffer_2
  Comparator #(.width(2)) comparator_5 (.a(2'b01), .b(counter_1_q), .eq(comparator_5_eq));  // open: gt, lt
  and and_1 (and_1_out, comparator_5_eq, comparator_3_eq);
  Adder adder_1 (.a({REG_A_q_2, REG_A_q}), .b({REG_B_q_2, REG_B_q}), .out(adder_1_out));  // open: cin, cout
  buf buffer_3 (pull_resistor_2_node, and_1_out);
  Comparator #(.width(2)) comparator_6 (.a(2'b01), .b(counter_1_q), .eq(comparator_6_eq));  // open: gt, lt
  and and_2 (and_2_out, comparator_6_eq, comparator_4_eq);
  Subtractor subtractor_1 (
    .a({REG_A_q_2, REG_A_q}), .b({REG_B_q_2, REG_B_q}), .out(subtractor_1_out));  // open: bin, bout
  buf buffer_4 (pull_resistor_2_node, and_2_out);

  // Notes on the sheet:
  //   buffer_1 drives only 1 and floats otherwise
  //   buffer_2 drives only 1 and floats otherwise
  //   contents of prog (hex, n*v repeats v):
  //   8*2 88*1
  //   buffer_3 drives only 1 and floats otherwise
  //   buffer_4 drives only 1 and floats otherwise
endmodule
