// Logisim project project.circ as structural Verilog: 1 circuit, main circuit main
module main (
  input  in_1,
  input  [1:0] in_2
);

  wire and_1_out, and_3_out, and_4_out, and_5_out, and_6_out, and_7_out, and_8_out, and_9_out, and_10_out,
       and_11_out, and_12_out, and_13_out, and_14_out, and_15_out, and_16_out, and_17_out, and_18_out,
       and_19_out, and_20_out, and_21_out, and_22_out, and_23_out, and_24_out, and_25_out, and_26_out,
       and_27_out, and_28_out, and_29_out, and_30_out, and_31_out, and_32_out, and_33_out, and_34_out,
       and_35_out, buffer_3_out, buffer_6_out, clock_1_out, comparator_1_eq, comparator_3_eq,
       comparator_4_eq, comparator_5_eq, comparator_6_eq, comparator_7_eq, comparator_7_lt, comparator_8_eq,
       comparator_9_eq, comparator_9_gt, comparator_10_eq, comparator_12_eq, comparator_14_eq,
       comparator_16_eq, comparator_17_eq, comparator_18_eq, comparator_19_eq, comparator_20_eq,
       comparator_21_eq, comparator_22_eq, comparator_23_eq, comparator_24_eq, comparator_25_eq,
       comparator_26_eq, comparator_27_eq, comparator_28_eq, comparator_29_eq, comparator_30_eq,
       comparator_31_eq, comparator_32_eq, comparator_33_eq, decoder_1_out0, decoder_1_out1, decoder_1_out2,
       decoder_1_out3, not_1_out, not_3_out, pc_carry, PORT_0_p5, pull_resistor_1_node, pull_resistor_3_node,
       pull_resistor_4_node, pull_resistor_5_node, pull_resistor_6_node, pull_resistor_8_node,
       pull_resistor_9_node, pull_resistor_10_node, pull_resistor_11_node, pull_resistor_13_node,
       pull_resistor_14_node, pull_resistor_16_node, RESET_out, STEP_out;
  wire [0:0] adder_1_cout, subtractor_1_bout;
  wire [1:0] counter_1_q, undriven;
  wire [1:1] pull_resistor_12_node;
  wire [6:0] REG_FLAGS_q_2;
  wire [7:0] adder_1_out, and_2_out, controlled_buffer_1_out, controlled_buffer_2_out,
       controlled_buffer_11_out, controlled_buffer_12_out, controlled_buffer_15_out,
       controlled_buffer_30_out, not_2_out, or_1_out, pc_q, pc_q_2, PORT_0_p1, PORT_0_p3, prog_data,
       ram_1_dout, REG_A_q, REG_B_q, REG_H_q, REG_L_q, register_1_q, subtractor_1_out, xor_1_out;
  wire [7:7] comparator_11_lt, comparator_13_gt, comparator_15_eq, or_2_out, or_3_out, REG_FLAGS_q;
  wire [15:0] controlled_buffer_14_out, controlled_buffer_21_out, controlled_buffer_33_out, PORT_0_p7;

  Clock clock_1 (.out(clock_1_out));
  Pull_Resistor pull_resistor_1 (.node(pull_resistor_1_node));
  buf buffer_1 (pull_resistor_1_node, clock_1_out);
  buf buffer_2 (pull_resistor_1_node, STEP_out);
  Button RESET (.out(RESET_out));
  Counter #(.max('h3), .width(2)) counter_1 (
    .clr(RESET_out), .load(pull_resistor_16_node), .clk(pull_resistor_1_node), .D(undriven), .Q(counter_1_q));  // open: up, count, carry
  Comparator #(.width(2)) comparator_1 (.a(2'b00), .b(counter_1_q), .eq(comparator_1_eq));  // open: gt, lt
  not not_1 (not_1_out, REG_FLAGS_q_2[0]);
  and and_1 (and_1_out, comparator_1_eq, not_1_out);
  Counter #(.max('hffff), .width(16)) pc (
    .clr(RESET_out), .load(pull_resistor_9_node), .clk(buffer_3_out), .D(controlled_buffer_21_out),
    .carry(pc_carry), .Q({pc_q_2, pc_q}));  // open: up, count
  buf buffer_3 (buffer_3_out, pull_resistor_14_node);
  buf buffer_4 (buffer_3_out, pull_resistor_9_node);
  Pull_Resistor pull_resistor_2 (.node(buffer_3_out));
  buf buffer_5 (buffer_3_out, and_1_out);
  LED overflow (.in(pc_carry));
  ROM #(.addrWidth(16)) prog (.addr({pc_q_2, pc_q}), .data(prog_data));
  Button STEP (.out(STEP_out));
  RAM #(.addrWidth(16), .clearpin("true"), .enables("line"), .\type ("nonvolatile")) ram_1 (
    .addr(controlled_buffer_14_out), .we(pull_resistor_8_node), .clk(pull_resistor_8_node),
    .din(controlled_buffer_15_out), .dout(ram_1_dout), .clr(RESET_out));
  Decoder #(.select(2)) decoder_1 (
    .out0(decoder_1_out0), .out1(decoder_1_out1), .out2(decoder_1_out2), .out3(decoder_1_out3), .sel(in_2),
    .en(in_1));
  Register register_1 (.D(prog_data), .clk(pull_resistor_11_node), .Q(register_1_q), .clr(RESET_out));  // open: en
  Register REG_A (.D(controlled_buffer_2_out), .clk(pull_resistor_3_node), .Q(REG_A_q), .clr(RESET_out));  // open: en
  LED led_1 (.in(pull_resistor_3_node));
  Register REG_B (.D(controlled_buffer_11_out), .clk(pull_resistor_4_node), .Q(REG_B_q), .clr(RESET_out));  // open: en
  LED led_2 (.in(pull_resistor_4_node));
  Register REG_H (.D(controlled_buffer_12_out), .clk(pull_resistor_5_node), .Q(REG_H_q), .clr(RESET_out));  // open: en
  LED led_3 (.in(pull_resistor_5_node));
  Register REG_L (.D(controlled_buffer_30_out), .clk(pull_resistor_6_node), .Q(REG_L_q), .clr(RESET_out));  // open: en
  LED led_4 (.in(pull_resistor_6_node));
  Register REG_FLAGS (
    .D(controlled_buffer_1_out), .clk(buffer_6_out), .Q({REG_FLAGS_q_2, REG_FLAGS_q[7]}), .clr(RESET_out));  // open: en
  assign controlled_buffer_1_out = pull_resistor_11_node ? {REG_FLAGS_q_2[6:1], 1'b0, REG_FLAGS_q[7]} : 8'bz;  // Controlled_Buffer controlled_buffer_1
  LED led_5 (.in(buffer_6_out));
  buf buffer_6 (buffer_6_out, pull_resistor_11_node);
  Pull_Resistor pull_resistor_3 (.node(pull_resistor_3_node));
  Pull_Resistor pull_resistor_4 (.node(pull_resistor_4_node));
  Pull_Resistor pull_resistor_5 (.node(pull_resistor_5_node));
  Pull_Resistor pull_resistor_6 (.node(pull_resistor_6_node));
  Pull_Resistor pull_resistor_7 (.node(buffer_6_out));
  Pull_Resistor pull_resistor_8 (.node(pull_resistor_8_node));
  Pull_Resistor pull_resistor_9 (.node(pull_resistor_9_node));
  Pull_Resistor pull_resistor_10 (.node(pull_resistor_10_node));
  Pull_Resistor pull_resistor_11 (.node(pull_resistor_11_node));
  Pull_Resistor pull_resistor_12 (.node(pull_resistor_12_node[1]));
  Pull_Resistor pull_resistor_13 (.node(pull_resistor_13_node));
  Pull_Resistor pull_resistor_14 (.node(pull_resistor_14_node));
  Pull_Resistor pull_resistor_15 (.node(register_1_q));
  Pull_Resistor pull_resistor_16 (.node(pull_resistor_16_node));
  buf buffer_7 (pull_resistor_3_node, and_8_out);
  buf buffer_8 (buffer_6_out, and_8_out);
  buf buffer_9 (pull_resistor_3_node, and_9_out);
  buf buffer_10 (buffer_6_out, and_9_out);
  assign controlled_buffer_2_out = comparator_6_eq ? {8{or_2_out[7]}} : 8'bz;  // Controlled_Buffer controlled_buffer_2
  assign controlled_buffer_2_out = comparator_8_eq ? {8{or_3_out[7]}} : 8'bz;  // Controlled_Buffer controlled_buffer_3
  assign controlled_buffer_2_out = comparator_10_eq ? {8{comparator_11_lt[7]}} : 8'bz;  // Controlled_Buffer controlled_buffer_4
  assign controlled_buffer_2_out = comparator_12_eq ? {8{comparator_13_gt[7]}} : 8'bz;  // Controlled_Buffer controlled_buffer_5
  assign controlled_buffer_2_out = comparator_14_eq ? {8{comparator_15_eq[7]}} : 8'bz;  // Controlled_Buffer controlled_buffer_6
  assign controlled_buffer_2_out = comparator_16_eq ? and_2_out : 8'bz;  // Controlled_Buffer controlled_buffer_7
  assign controlled_buffer_2_out = comparator_17_eq ? or_1_out : 8'bz;  // Controlled_Buffer controlled_buffer_8
  assign controlled_buffer_2_out = comparator_18_eq ? xor_1_out : 8'bz;  // Controlled_Buffer controlled_buffer_9
  assign controlled_buffer_2_out = comparator_19_eq ? not_2_out : 8'bz;  // Controlled_Buffer controlled_buffer_10
  assign controlled_buffer_11_out = comparator_20_eq ? pc_q : 8'bz;  // Controlled_Buffer controlled_buffer_11
  assign controlled_buffer_12_out = comparator_20_eq ? pc_q_2 : 8'bz;  // Controlled_Buffer controlled_buffer_12
  assign controlled_buffer_2_out = comparator_21_eq ? {8{REG_FLAGS_q[7]}} : 8'bz;  // Controlled_Buffer controlled_buffer_13
  buf buffer_11 (pull_resistor_14_node, and_3_out);
  buf buffer_12 (pull_resistor_14_node, and_4_out);
  buf buffer_13 (pull_resistor_14_node, and_5_out);
  buf buffer_14 (pull_resistor_14_node, and_6_out);
  assign controlled_buffer_14_out = comparator_31_eq ? {REG_H_q, REG_L_q} : 16'bz;  // Controlled_Buffer controlled_buffer_14
  assign controlled_buffer_15_out = comparator_31_eq ? REG_A_q : 8'bz;  // Controlled_Buffer controlled_buffer_15
  buf buffer_15 (pull_resistor_8_node, and_33_out);
  assign controlled_buffer_14_out = comparator_32_eq ? {REG_H_q, REG_L_q} : 16'bz;  // Controlled_Buffer controlled_buffer_16
  buf buffer_16 (pull_resistor_3_node, and_34_out);
  Comparator #(.width(2)) comparator_2 (.a(2'b00), .b(counter_1_q), .eq(pull_resistor_10_node));  // open: gt, lt
  Comparator comparator_3 (.a(register_1_q), .b({8{1'b0}}), .eq(comparator_3_eq));  // open: gt, lt
  LED NOP (.in(comparator_3_eq));
  Comparator comparator_4 (.a(register_1_q), .b(8'h1), .eq(comparator_4_eq));  // open: gt, lt
  LED ADD (.in(comparator_4_eq));
  assign controlled_buffer_2_out = and_8_out ? adder_1_out : 8'bz;  // Controlled_Buffer controlled_buffer_17
  assign controlled_buffer_1_out = and_8_out ? {REG_FLAGS_q_2, adder_1_cout[0]} : 8'bz;  // Controlled_Buffer controlled_buffer_18
  Comparator comparator_5 (.a(register_1_q), .b(8'h2), .eq(comparator_5_eq));  // open: gt, lt
  LED SUB (.in(comparator_5_eq));
  assign controlled_buffer_2_out = and_9_out ? subtractor_1_out : 8'bz;  // Controlled_Buffer controlled_buffer_19
  assign controlled_buffer_1_out = and_9_out ? {REG_FLAGS_q_2, subtractor_1_bout[0]} : 8'bz;  // Controlled_Buffer controlled_buffer_20
  Comparator comparator_6 (.a(register_1_q), .b(8'h10), .eq(comparator_6_eq));  // open: gt, lt
  LED LTEQ (.in(comparator_6_eq));
  Comparator #(.mode("unsigned")) comparator_7 (
    .a(REG_A_q), .b(REG_B_q), .eq(comparator_7_eq), .lt(comparator_7_lt));  // open: gt
  Comparator comparator_8 (.a(register_1_q), .b(8'h11), .eq(comparator_8_eq));  // open: gt, lt
  LED GTEQ (.in(comparator_8_eq));
  Comparator #(.mode("unsigned")) comparator_9 (
    .a(REG_A_q), .b(REG_B_q), .gt(comparator_9_gt), .eq(comparator_9_eq));  // open: lt
  Comparator comparator_10 (.a(register_1_q), .b(8'h12), .eq(comparator_10_eq));  // open: gt, lt
  LED LT (.in(comparator_10_eq));
  Comparator #(.mode("unsigned")) comparator_11 (.a(REG_A_q), .b(REG_B_q), .lt(comparator_11_lt[7]));  // open: gt, eq
  Comparator comparator_12 (.a(register_1_q), .b(8'h13), .eq(comparator_12_eq));  // open: gt, lt
  LED GT (.in(comparator_12_eq));
  Comparator #(.mode("unsigned")) comparator_13 (.a(REG_A_q), .b(REG_B_q), .gt(comparator_13_gt[7]));  // open: eq, lt
  Comparator comparator_14 (.a(register_1_q), .b(8'h14), .eq(comparator_14_eq));  // open: gt, lt
  LED EQ (.in(comparator_14_eq));
  Comparator #(.mode("unsigned")) comparator_15 (.a(REG_A_q), .b(REG_B_q), .eq(comparator_15_eq[7]));  // open: gt, lt
  Comparator comparator_16 (.a(register_1_q), .b(8'h20), .eq(comparator_16_eq));  // open: gt, lt
  LED AND_BITWISE (.in(comparator_16_eq));
  assign and_2_out = REG_A_q & REG_B_q;  // AND_Gate and_2, 8 bits wide
  Comparator comparator_17 (.a(register_1_q), .b(8'h21), .eq(comparator_17_eq));  // open: gt, lt
  LED OR_BITWISE (.in(comparator_17_eq));
  assign or_1_out = REG_A_q | REG_B_q;  // OR_Gate or_1, 8 bits wide
  Comparator comparator_18 (.a(register_1_q), .b(8'h22), .eq(comparator_18_eq));  // open: gt, lt
  LED XOR_BITWISE (.in(comparator_18_eq));
  assign xor_1_out = REG_A_q ^ REG_B_q;  // XOR_Gate xor_1, 8 bits wide
  Comparator comparator_19 (.a(register_1_q), .b(8'h23), .eq(comparator_19_eq));  // open: gt, lt
  LED NOT_BITWISE (.in(comparator_19_eq));
  assign not_2_out = ~REG_A_q;  // NOT_Gate not_2, 8 bits wide
  Comparator comparator_20 (.a(register_1_q), .b(8'h30), .eq(comparator_20_eq));  // open: gt, lt
  LED GET_PC (.in(comparator_20_eq));
  buf buffer_17 (pull_resistor_5_node, and_19_out);
  buf buffer_18 (pull_resistor_4_node, and_19_out);
  Comparator comparator_21 (.a(register_1_q), .b(8'h31), .eq(comparator_21_eq));  // open: gt, lt
  LED GET_CARRY (.in(comparator_21_eq));
  Comparator comparator_22 (.a(register_1_q), .b(8'h40), .eq(comparator_22_eq));  // open: gt, lt
  LED JUMP (.in(comparator_22_eq));
  buf buffer_19 (pull_resistor_9_node, and_21_out);
  assign controlled_buffer_21_out = and_21_out ? {REG_H_q, REG_L_q} : 16'bz;  // Controlled_Buffer controlled_buffer_21
  assign controlled_buffer_1_out = and_22_out ? {REG_FLAGS_q_2[6:1], pull_resistor_12_node[1], REG_FLAGS_q[7]} : 8'bz;  // Controlled_Buffer controlled_buffer_22
  buf buffer_20 (buffer_6_out, and_22_out);
  Comparator comparator_23 (.a(register_1_q), .b(8'h41), .eq(comparator_23_eq));  // open: gt, lt
  LED JUMPI (.in(comparator_23_eq));
  Comparator comparator_24 (.a({8{1'b1}}), .b(REG_A_q), .eq(comparator_24_eq));  // open: gt, lt
  buf buffer_21 (pull_resistor_9_node, and_24_out);
  assign controlled_buffer_21_out = and_24_out ? {REG_H_q, REG_L_q} : 16'bz;  // Controlled_Buffer controlled_buffer_23
  assign controlled_buffer_1_out = and_25_out ? {REG_FLAGS_q_2[6:1], pull_resistor_12_node[1], REG_FLAGS_q[7]} : 8'bz;  // Controlled_Buffer controlled_buffer_24
  buf buffer_22 (buffer_6_out, and_25_out);
  Comparator comparator_25 (.a(register_1_q), .b(8'h42), .eq(comparator_25_eq));  // open: gt, lt
  LED JUMPZ (.in(comparator_25_eq));
  Comparator comparator_26 (.a({8{1'b0}}), .b(REG_A_q), .eq(comparator_26_eq));  // open: gt, lt
  buf buffer_23 (pull_resistor_9_node, and_27_out);
  assign controlled_buffer_21_out = and_27_out ? {REG_H_q, REG_L_q} : 16'bz;  // Controlled_Buffer controlled_buffer_25
  assign controlled_buffer_1_out = and_28_out ? {REG_FLAGS_q_2[6:1], pull_resistor_12_node[1], REG_FLAGS_q[7]} : 8'bz;  // Controlled_Buffer controlled_buffer_26
  buf buffer_24 (buffer_6_out, and_28_out);
  Comparator comparator_27 (.a(register_1_q), .b(8'h60), .eq(comparator_27_eq));  // open: gt, lt
  LED LDA (.in(comparator_27_eq));
  and and_3 (and_3_out, pull_resistor_12_node[1], comparator_27_eq);
  buf buffer_25 (pull_resistor_3_node, and_29_out);
  assign controlled_buffer_2_out = and_29_out ? prog_data : 8'bz;  // Controlled_Buffer controlled_buffer_27
  Comparator comparator_28 (.a(register_1_q), .b(8'h61), .eq(comparator_28_eq));  // open: gt, lt
  LED LDB (.in(comparator_28_eq));
  and and_4 (and_4_out, pull_resistor_12_node[1], comparator_28_eq);
  buf buffer_26 (pull_resistor_4_node, and_30_out);
  assign controlled_buffer_11_out = and_30_out ? prog_data : 8'bz;  // Controlled_Buffer controlled_buffer_28
  Comparator comparator_29 (.a(register_1_q), .b(8'h62), .eq(comparator_29_eq));  // open: gt, lt
  LED LDC (.in(comparator_29_eq));
  and and_5 (and_5_out, pull_resistor_12_node[1], comparator_29_eq);
  buf buffer_27 (pull_resistor_5_node, and_31_out);
  assign controlled_buffer_12_out = and_31_out ? prog_data : 8'bz;  // Controlled_Buffer controlled_buffer_29
  Comparator comparator_30 (.a(register_1_q), .b(8'h63), .eq(comparator_30_eq));  // open: gt, lt
  LED LDD (.in(comparator_30_eq));
  and and_6 (and_6_out, pull_resistor_12_node[1], comparator_30_eq);
  buf buffer_28 (pull_resistor_6_node, and_32_out);
  assign controlled_buffer_30_out = and_32_out ? prog_data : 8'bz;  // Controlled_Buffer controlled_buffer_30
  Comparator comparator_31 (.a(register_1_q), .b(8'h90), .eq(comparator_31_eq));  // open: gt, lt
  LED MSET (.in(comparator_31_eq));
  Comparator comparator_32 (.a(register_1_q), .b(8'h91), .eq(comparator_32_eq));  // open: gt, lt
  LED MLOAD (.in(comparator_32_eq));
  assign controlled_buffer_2_out = comparator_32_eq ? ram_1_dout : 8'bz;  // Controlled_Buffer controlled_buffer_31
  Comparator comparator_33 (.a(register_1_q), .b(8'h50), .eq(comparator_33_eq));  // open: gt, lt
  LED RI (.in(comparator_33_eq));
  buf buffer_29 (pull_resistor_3_node, and_35_out);
  not not_3 (not_3_out, REG_B_q[0]);
  and and_7 (and_7_out, not_3_out, and_35_out);
  assign controlled_buffer_2_out = and_7_out ? PORT_0_p1 : 8'bz;  // Controlled_Buffer controlled_buffer_32
  Comparator #(.width(2)) comparator_34 (.a(2'b01), .b(counter_1_q), .eq(pull_resistor_11_node));  // open: gt, lt
  and and_8 (and_8_out, pull_resistor_12_node[1], comparator_4_eq);
  Adder adder_1 (.a(REG_A_q), .b(REG_B_q), .out(adder_1_out), .cout(adder_1_cout[0]));  // open: cin
  and and_9 (and_9_out, pull_resistor_12_node[1], comparator_5_eq);
  Subtractor subtractor_1 (.a(REG_A_q), .b(REG_B_q), .out(subtractor_1_out), .bout(subtractor_1_bout[0]));  // open: bin
  or or_2 (or_2_out[7], comparator_7_eq, comparator_7_lt);
  and and_10 (and_10_out, pull_resistor_12_node[1], comparator_6_eq);
  buf buffer_30 (pull_resistor_3_node, and_10_out);
  or or_3 (or_3_out[7], comparator_9_gt, comparator_9_eq);
  and and_11 (and_11_out, pull_resistor_12_node[1], comparator_8_eq);
  buf buffer_31 (pull_resistor_3_node, and_11_out);
  and and_12 (and_12_out, pull_resistor_12_node[1], comparator_10_eq);
  buf buffer_32 (pull_resistor_3_node, and_12_out);
  and and_13 (and_13_out, pull_resistor_12_node[1], comparator_12_eq);
  buf buffer_33 (pull_resistor_3_node, and_13_out);
  and and_14 (and_14_out, pull_resistor_12_node[1], comparator_14_eq);
  buf buffer_34 (pull_resistor_3_node, and_14_out);
  and and_15 (and_15_out, pull_resistor_12_node[1], comparator_16_eq);
  buf buffer_35 (pull_resistor_3_node, and_15_out);
  and and_16 (and_16_out, pull_resistor_12_node[1], comparator_17_eq);
  buf buffer_36 (pull_resistor_3_node, and_16_out);
  and and_17 (and_17_out, pull_resistor_12_node[1], comparator_18_eq);
  buf buffer_37 (pull_resistor_3_node, and_17_out);
  and and_18 (and_18_out, pull_resistor_12_node[1], comparator_19_eq);
  buf buffer_38 (pull_resistor_3_node, and_18_out);
  and and_19 (and_19_out, pull_resistor_12_node[1], comparator_20_eq);
  and and_20 (and_20_out, pull_resistor_12_node[1], comparator_21_eq);
  buf buffer_39 (pull_resistor_3_node, and_20_out);
  and and_21 (and_21_out, pull_resistor_13_node, comparator_22_eq);
  and and_22 (and_22_out, pull_resistor_12_node[1], comparator_22_eq);
  and and_23 (and_23_out, comparator_23_eq, comparator_24_eq);
  and and_24 (and_24_out, pull_resistor_13_node, and_23_out);
  and and_25 (and_25_out, pull_resistor_12_node[1], and_23_out);
  and and_26 (and_26_out, comparator_25_eq, comparator_26_eq);
  and and_27 (and_27_out, pull_resistor_13_node, and_26_out);
  and and_28 (and_28_out, pull_resistor_12_node[1], and_26_out);
  and and_29 (and_29_out, pull_resistor_13_node, comparator_27_eq);
  and and_30 (and_30_out, pull_resistor_13_node, comparator_28_eq);
  and and_31 (and_31_out, pull_resistor_13_node, comparator_29_eq);
  and and_32 (and_32_out, pull_resistor_13_node, comparator_30_eq);
  and and_33 (and_33_out, comparator_31_eq, pull_resistor_13_node);
  and and_34 (and_34_out, comparator_32_eq, pull_resistor_13_node);
  and and_35 (and_35_out, pull_resistor_13_node, comparator_33_eq);
  Comparator #(.width(2)) comparator_35 (.a(2'b10), .b(counter_1_q), .eq(pull_resistor_12_node[1]));  // open: gt, lt
  assign controlled_buffer_33_out = PORT_0_p5 ? {16{1'b1}} : 16'bz;  // Controlled_Buffer controlled_buffer_33
  Comparator #(.width(2)) comparator_36 (.a(2'b11), .b(counter_1_q), .eq(pull_resistor_13_node));  // open: gt, lt
  // PortIO #(.direction("IOMultiEnable"), .number(16)) PORT_0: pin names not known; wires that end beside it: PORT_0_p1, PORT_0_p1, PORT_0_p3, PORT_0_p3, PORT_0_p5, PORT_0_p5, PORT_0_p7, REG_B_q[0]
  assign PORT_0_p7 = 16'hff & controlled_buffer_33_out;  // AND_Gate and_36, 16 bits wide

  // Notes on the sheet:
  //   buffer_1 drives only 1 and floats otherwise
  //   buffer_2 drives only 1 and floats otherwise
  //   buffer_3 drives only 1 and floats otherwise
  //   buffer_4 drives only 1 and floats otherwise
  //   buffer_5 drives only 1 and floats otherwise
  //   contents of prog (hex, n*v repeats v):
  //   60 10 90 63 1 60 20 90 63 2 60 ff 90 63 1 91 61 20 14 62 0 63 0 41
  //   buffer_6 drives only 1 and floats otherwise
  //   buffer_7 drives only 1 and floats otherwise
  //   buffer_8 drives only 1 and floats otherwise
  //   buffer_9 drives only 1 and floats otherwise
  //   buffer_10 drives only 1 and floats otherwise
  //   buffer_11 drives only 1 and floats otherwise
  //   buffer_12 drives only 1 and floats otherwise
  //   buffer_13 drives only 1 and floats otherwise
  //   buffer_14 drives only 1 and floats otherwise
  //   buffer_15 drives only 1 and floats otherwise
  //   buffer_16 drives only 1 and floats otherwise
  //   buffer_17 drives only 1 and floats otherwise
  //   buffer_18 drives only 1 and floats otherwise
  //   buffer_19 drives only 1 and floats otherwise
  //   buffer_20 drives only 1 and floats otherwise
  //   buffer_21 drives only 1 and floats otherwise
  //   buffer_22 drives only 1 and floats otherwise
  //   buffer_23 drives only 1 and floats otherwise
  //   buffer_24 drives only 1 and floats otherwise
  //   buffer_25 drives only 1 and floats otherwise
  //   buffer_26 drives only 1 and floats otherwise
  //   buffer_27 drives only 1 and floats otherwise
  //   buffer_28 drives only 1 and floats otherwise
  //   buffer_29 drives only 1 and floats otherwise
  //   buffer_30 drives only 1 and floats otherwise
  //   buffer_31 drives only 1 and floats otherwise
  //   buffer_32 drives only 1 and floats otherwise
  //   buffer_33 drives only 1 and floats otherwise
  //   buffer_34 drives only 1 and floats otherwise
  //   buffer_35 drives only 1 and floats otherwise
  //   buffer_36 drives only 1 and floats otherwise
  //   buffer_37 drives only 1 and floats otherwise
  //   buffer_38 drives only 1 and floats otherwise
  //   buffer_39 drives only 1 and floats otherwise
endmodule
